# Fritzing sketch Cabinet (saved by Fritzing 0.9.3b)

parts:
  Part1 = Arduino Pro Mini v13
  Power_plug1 = Power plug
  J1 = Screw terminal - 2 pins [package=THT]
  J2 = Screw terminal - 2 pins [package=THT]
  J3 = Screw terminal - 2 pins [package=THT]

nets:
  N1: Part1.RAW, Power_plug1.VCC, J1.pin1
  GND: Part1.GND, Power_plug1.GND, J1.pin2
  N2: Part1.VCC, J2.pin1
  N3: Part1.D4, J3.pin2
  N4: Part1.D3_PWM, J3.pin1
  N5: Part1.D2, J2.pin2

notes:
  12V
